// Logisim project sample.circ as structural Verilog: 1 circuit, main circuit main
module main (
  output [31:0] RD1,
  output [31:0] RD2,
  output halt
);

  wire clock_1_out;
  wire [7:0] counter_1_q;
  wire [31:0] rom_1_data, rom_2_data;

  Counter counter_1 (.Q(counter_1_q), .carry(halt), .clk(clock_1_out));  // open: load, D, count, clr
  Clock clock_1 (.out(clock_1_out));
  ROM #(.dataWidth(32)) rom_1 (.addr(counter_1_q), .data(rom_1_data));  // open: sel
  ROM #(.dataWidth(32)) rom_2 (.addr(counter_1_q), .data(rom_2_data));  // open: sel
  grf_sample grf_sample_1 (
    .A1(rom_2_data[14:10]), .A2(rom_2_data[9:5]), .A3(rom_2_data[4:0]), .WD(rom_1_data), .clk(clock_1_out),
    .reset(1'b0), .WE(rom_2_data[15]), .RD1(RD1), .RD2(RD2));

  // Notes on the sheet:
  //   contents of rom_1 (hex, n*v repeats v):
  //   14eff542 34937f4f 9537eca1 c27d5c9a 4f66e5b c9cc319a 1df714f6 7bb1465f 9c0169fa 3b951e44 420d5178
  //   8446663 6d44c5 40499f80 bdbaa618 d94066 d30067b1 a5efeba9 4ce2c16f 6da1bc5f 1c68712a 7ed37dc9
  //   23aae30f d822b5ca 249590ab 79e33ba 5ba7bd90 8b7926fc dd468707 88d6dcc7 a4ee2939 48864ecf af4fee8d
  //   7267a6e1 503e7b63 9f6dcb24 6e405304 c78d603 78aaf79e bca32531 31bf72 4ce6c08 41173bb4 9ab8ea6a
  //   daf104c2 9ca40497 88185c1f 35a04b1b e9a1d56d 5efcff7 110d8f09 3d0e0d60 b85bd21d b1cd3a4b eab64714
  //   e5ee3016 2189024e 8cf6ab51 65badc6b 28315864 e3afafe9 c86130b7 824ca908 8dc7435 a3d070f5 23d1d36e
  //   2a1ef497 bbf705b e454a12c 3460ae62 3780fdc5 19a2356a 5e8ea1ae 883d10d1 d60e101b bb32cb40 f31cef2
  //   b1695c1c 901a3a93 b56b6962 6ebac87d b983c221 3b08c9fe 59a04722 f1d80649 30538611 ee13fe39 196a94fb
  //   f11df967 bbc1dcd3 1dfdde79 1808648c a1df0146 66b656b6 2f1eb01f e204b920 51165197 809f354a e020674d
  //   84fd58d0
  //   contents of rom_2 (hex, n*v repeats v):
  //   c5a56264 df950c4 e545fa4c ec3fe09 494a3c0c 62d43a7a 6f296429 26068afe d073f8e9 c21f402e ae9f5b61
  //   3230bef2 9438a815 da33a298 dee7696 96154326 b09daf63 bcbbed81 841cbb59 3fed0c9f 501c4b8 e9f9cef1
  //   13711352 6a045e1b 6f1fa5d2 fa5fa09b 7e6dc9e3 c94df16f 31162110 b5d15e00 f1b6db1e 2092a174 9f8c6c2e
  //   d51704b4 7de38635 4015d829 af78fb5a 5455c2d4 f4aad68d a58822d0 7819538d 836466b9 9a20382a f8f6e3a6
  //   3111b607 406c5beb c00b5109 118ccd6b bd91dbff 236dc4c1 ad31d264 f59845d8 faf09907 49f1a93d 1e55497
  //   67656703 790bd77e 93510091 ebeef77f a56453aa 701712a3 8f3627ba 23741076 d5412f7f 168292fe bfafafae
  //   f5f67ebd 39fcced4 d3c2933 8560a72e 898ee49 cedf7121 ddc8d71c d62312ea 862fdbc5 c11097b 9437c5a9
  //   82d6709b 14b70372 6cdf0fd3 18958ccd ace0d0a5 15d77ba7 5f41f2a5 37c9c962 dd6052e2 4c5a822f ef3db566
  //   749de0d2 c64bf8d1 aafd19d8 febcd419 443f5faa 886ff4d 835b2a69 44c774f3 2bf79206 ad36e52f 51804610
  //   ce368ec9
  //   reset
  //   clk
  //   write_en
endmodule
